// Logisim project sistema_de_conteo.circ as structural Verilog
module main (
);

  wire button_1_out, maquina_nueve_1_clock_out, undriven, undriven_2;
  wire [3:0] contador_1_output, contador_2_output;
  wire [6:0] bcd_display_1_salida_display, bcd_display_2_salida_display;

  Clock clock_1 ();  // open: out
  Button button_1 (.out(button_1_out));
  maquina_nueve maquina_nueve_1 (
    .clock_in(undriven), .reset(button_1_out), .entrada_cuenta(contador_1_output),
    .clock_out(maquina_nueve_1_clock_out));
  contador contador_1 (.clock(undriven_2), .reset(button_1_out), .\output (contador_1_output));
  contador contador_2 (.clock(maquina_nueve_1_clock_out), .reset(button_1_out), .\output (contador_2_output));
  bcd_display bcd_display_1 (.entrada_binaria(contador_1_output), .salida_display(bcd_display_1_salida_display));
  bcd_display bcd_display_2 (
    .entrada_binaria(contador_2_output),
    .salida_display({{2{bcd_display_2_salida_display[6]}}, bcd_display_2_salida_display[4:0]}));
  _7_Segment_Display u_7_segment_display_1 (
    .g(bcd_display_1_salida_display[0]), .f(bcd_display_1_salida_display[1]),
    .a(bcd_display_1_salida_display[6]), .b(bcd_display_1_salida_display[5]),
    .e(bcd_display_1_salida_display[2]), .d(bcd_display_1_salida_display[3]),
    .c(bcd_display_1_salida_display[4]));  // open: dp
  _7_Segment_Display u_7_segment_display_2 (
    .g(bcd_display_2_salida_display[0]), .f(bcd_display_2_salida_display[1]),
    .a(bcd_display_2_salida_display[6]), .b(bcd_display_2_salida_display[6]));  // open: e, d, c, dp
endmodule

// VHDL entity contador, as the project stores it:
--------------------------------------------------------------------------------
-- Project : Sistema de conteo
-- File    :
-- Autor   :Gustavo A. Castrillón	
-- Date    :03/15/2023
--
--------------------------------------------------------------------------------
-- Description : Vamos a hacer un sistema de conteo desde 0 hasta 9 puntos,por esto, necesitamos una cantidad de 4 bits  
--
--------------------------------------------------------------------------------

LIBRARY ieee;
USE ieee.std_logic_1164.all;


ENTITY contador IS
  PORT (
  ------------------------------------------------------------------------------
  --Insert input ports below
    clock      : IN  std_logic;                    -- input bit example
    --Nreset 	: IN  std_logic; --Es comun que todo sistema que empiece con N es una logica negada. 
    --NOTA: Consume menos potencia el bajar una señal a cero que subirla a 1. 
    reset 	: IN  std_logic; 
    output	: OUT std_logic_vector(3 downto 0)
    );
END contador;

--------------------------------------------------------------------------------
--Complete your VHDL description below
--------------------------------------------------------------------------------

ARCHITECTURE TypeArchitecture OF contador IS
	signal cuenta : std_logic_vector(3 downto 0); 
BEGIN
process(clock,reset)
begin
	if reset = '1' then
		cuenta <= "0000"; 
	--rising_edge es un flanco de subida luego no hay que colocar 
	--elsif clock = '1' and clock'event then 
	elsif rising_edge(clock) then
		if cuenta>="1001" then
			cuenta<="0000"; 
		else
			cuenta<= cuenta + 1; 
		end if; 
	end if;
end process; 	

END TypeArchitecture;

// VHDL entity bcd_display, as the project stores it:
--------------------------------------------------------------------------------
-- Project :Display el cual me mostrara en un pantalla los numeros contados 
-- File    :
-- Autor   :
-- Date    :
--
--------------------------------------------------------------------------------
-- Description :
--
--------------------------------------------------------------------------------

LIBRARY ieee;
USE ieee.std_logic_1164.all;

ENTITY bcd_display IS
  PORT (
  	entrada_binaria 	: IN 	std_logic_vector(3 downto 0); 
  	salida_display 	: OUT 	std_logic_vector(6 downto 0)
    );
END bcd_display;

--------------------------------------------------------------------------------
--Complete your VHDL description below
--------------------------------------------------------------------------------

ARCHITECTURE TypeArchitecture OF bcd_display IS

BEGIN
salida_display <= "1111110" when entrada_display = "0000" else
			   "0110000" when entrada_display = "0001" else
			   "1101101" when entrada_display = "0010" else
			   "1111001" when entrada_display = "0011" else
			   "0110011" when entrada_display = "0100" else
			   "1011011" when entrada_display = "0101" else
			   "0011111" when entrada_display = "0110" else
			   "1110000" when entrada_display = "0111" else
			   "1111111" when entrada_display = "1000" else
			   "1110011" when entrada_display = "1001" else
			   "0000000";
			   


END TypeArchitecture;

// VHDL entity maquina_nueve, as the project stores it:
--------------------------------------------------------------------------------
-- Project :
-- File    :
-- Autor   :
-- Date    :
--
--------------------------------------------------------------------------------
-- Description :
--
--------------------------------------------------------------------------------

LIBRARY ieee;
USE ieee.std_logic_1164.all;

ENTITY maquina_nueve IS
  PORT (
  ------------------------------------------------------------------------------
  --Insert input ports below
    clock_in      : IN  std_logic;                    -- input bit example
    clock_out 	: OUT std_logic; 
    reset 	: IN	 std_logic; 
    entrada_cuenta	: IN std_logic_vector(3 downto 0) --output vector example
    );
END maquina_nueve;

--------------------------------------------------------------------------------
--Complete your VHDL description below
--------------------------------------------------------------------------------

ARCHITECTURE TypeArchitecture OF maquina_nueve IS
type estados_cuenta is (s0,s1); 
signal estados : estados_cuenta; 

BEGIN

process(clock_in, reset) 
begin 	
--Es importante a la hora de instanciar considerar el mismo reset par todos los datos. 
	if reset = '1' then 
		clock_out <= '0'; 
		estados <= s0; 
	elsif rising_edge(clock_in) then 
		case estados is
		when s0 =>
			clock_out <= '0'; 
			if entrada_cuenta >= "1001" then 
				estados <= s1; 
			end if; 
		when s1 => 
			if entrada_cuenta >="0000" then 
				estados <=s0;  
				clock_out <= '1'; 
			end if; 
		when others =>
			clock_out<='0'; 
			estados <= s0; 
		end case; 
	end if; 
end process; 	

END TypeArchitecture;

// VHDL entity displays_2, as the project stores it:
--------------------------------------------------------------------------------
-- Project :
-- File    :
-- Autor   :
-- Date    :
--
--------------------------------------------------------------------------------
-- Description :
--
--------------------------------------------------------------------------------

LIBRARY ieee;
USE ieee.std_logic_1164.all;

ENTITY displays_2 IS
  PORT (
  ------------------------------------------------------------------------------
  --Insert input ports below
    clock2      : IN  std_logic;                    -- input bit example
    reset		: IN  std_logic; 

    display_1 	: OUT std_logic_vector(6 downto 0); 
    display_2 	: OUT std_logic_vector(6 downto 0); 
    );
END displays_2;

--------------------------------------------------------------------------------
--Complete your VHDL description below
--------------------------------------------------------------------------------
--Instanciado de los elementos generados 
ARCHITECTURE TypeArchitecture OF displays_2 IS

component contador IS
  PORT (
  ------------------------------------------------------------------------------
  --Insert input ports below
    clock      : IN  std_logic;                    -- input bit example
    --Nreset 	: IN  std_logic; --Es comun que todo sistema que empiece con N es una logica negada. 
    --NOTA: Consume menos potencia el bajar una señal a cero que subirla a 1. 
    reset 	: IN  std_logic; 
    output	: OUT std_logic_vector(3 downto 0)
    );
END component;

component bcd_display IS
  PORT (
  	entrada_binaria 	: IN 	std_logic_vector(3 downto 0); 
  	salida_display 	: OUT 	std_logic_vector(6 downto 0)
    );
END component;

component maquina_nueve IS
  PORT (
  ------------------------------------------------------------------------------
  --Insert input ports below
    clock_in      : IN  std_logic;                    -- input bit example
    clock_out 	: OUT std_logic; 
    reset 	: IN	 std_logic; 
    entrada_cuenta	: IN std_logic_vector(3 downto 0) --output vector example
    );
END component;

signal bcd_1 : std_logic_vector(3 downto 0); 
signal bcd_2 : std_logic_vector(3 downto 0); 
signal display_int : std_logic_vector(6 downto 0); 
signal clk_int : std_logic
BEGIN
--union de las señales dentro de la fpga
cuenta1: contador
  PORT map (
  ------------------------------------------------------------------------------
  --Insert input ports below
    clock   => clock2, 
    reset => reset,
    output => bdc_1
    --también puedo escribirlo de la forma: 
    --clock2,
    --reset,
    --bdc_1
    --Pero esto puede hacer que uno se pierda en el texto. 
    ); 
disp_1 : bcd_display 
  PORT map(
  	entrada_binaria => bcd_1, 
  	salida_display => display_int
    );
    
mq9: maquina_nueve 
  PORT map(
  ------------------------------------------------------------------------------
  --Insert input ports below
    clock_in   => clock2,   
    clock_out  => clk_int,
    reset 	 => reset,
    entrada_cuenta	=> display_1
    );
    
cuenta2: contador
  PORT map (
  ------------------------------------------------------------------------------
  --Insert input ports below
    clock   => clk_int, 
    reset => reset,
    output => bdc_2
    --también puedo escribirlo de la forma: 
    --clock2,
    --reset,
    --bdc_1
    --Pero esto puede hacer que uno se pierda en el texto. 
    ); 
disp_2 : bcd_display 
  PORT map(
  	entrada_binaria => bcd_2, 
  	salida_display => display_2
    );

END TypeArchitecture;
