// Logisim project motor_de_paso.circ as structural Verilog
module main (
);

  wire button_1_out, clock_1_out, dipswitch_1_sw1;
  wire [2:0] dipswitch_1_sw2;
  wire [3:0] motor_1_salida;

  DipSwitch dipswitch_1 (
    .sw1(dipswitch_1_sw1), .sw2(dipswitch_1_sw2[0]), .sw3(dipswitch_1_sw2[1]), .sw4(dipswitch_1_sw2[2]));  // open: sw5, sw6, sw7, sw8
  Button button_1 (.out(button_1_out));
  Clock clock_1 (.out(clock_1_out));
  motor motor_1 (
    .clock(clock_1_out), .enable(dipswitch_1_sw1), .reset(button_1_out), .selector(dipswitch_1_sw2),
    .salida(motor_1_salida));
  LED led_1 (.in(motor_1_salida[0]));
  LED led_2 (.in(motor_1_salida[1]));
  LED led_3 (.in(motor_1_salida[2]));
  LED led_4 (.in(motor_1_salida[3]));
endmodule

// VHDL entity motor, as the project stores it:
--------------------------------------------------------------------------------
-- Project : Motor de paso 
-- File    :
-- Autor   : Gustavo A. Castrillón 
-- Date    : 03-08-2023
--
--------------------------------------------------------------------------------
-- Description : Creación de un motor de paso por medio de compuertas logicas 
--
--------------------------------------------------------------------------------

LIBRARY ieee;
USE ieee.std_logic_1164.all;

ENTITY motor IS
  PORT (
  ------------------------------------------------------------------------------
  --Insert input ports below
    clock      : IN  std_logic;                    -- input bit example
    enable 	: IN std_logic; 

    reset 	: in std_logic; 
    selector 	: in std_logic_vector(2 downto 0); 
    salida 	: out std_logic_vector(3 downto 0)
    );
END motor;

--------------------------------------------------------------------------------
--Complete your VHDL description below
--------------------------------------------------------------------------------


-- "000" -> S0 -> S1 -> S2 -> S3 -> S4 -> S5 -> S6 -> S7 
-- "001" -> S0 -> S2 -> S4 -> S6
-- "010" -> S1 -> S3 -> S5 -> S7 

ARCHITECTURE TypeArchitecture OF motor IS
	type estados_motor is (s0, s1, s2, s3, s4, s5, s6, s7);
	signal estado_actual : estados_motor;
	
BEGIN
	motor1: process(clock,reset)
	begin 
		if reset = '1' then
			estado_actual <= s0; 
			salida <= "0000"; 
		elsif rising_edge(clock) then
			case estado_actual is 
			 	when s0 => 
			 		if enable = '1' then
			 			salida <= "0001";
			 			case selector is
			 			when "000" => estado_actual <= s1; 
			 			when "001" => estado_actual <= s2; 
			 			when "010" => estado_actual <= s1; 
			 			when "100" => estado_actual <= s7; 
			 			when "101" => estado_actual <= s6; 
			 			when "110" => estado_actual <= s7; 
			 			when others => null; 
			 			end case; 
					else 
						salida <= "0000";
						estado_actual <= estado_actual;  
					end if; 

				when s1 => 
			 		if enable = '1' then
			 			salida <= "0011";
			 			case selector is
			 			when "000" => estado_actual <= s2; 
			 			when "001" => estado_actual <= s2; 
			 			when "010" => estado_actual <= s3; 
			 			when "100" => estado_actual <= s0; 
			 			when "101" => estado_actual <= s6; 
			 			when "110" => estado_actual <= s7; 
			 			when others => null; 
			 			end case; 
					else 
						salida <= "0000";
						estado_actual <= s0;  
					end if; 
				
				when s2 => 
			 		if enable = '1' then
			 			salida <= "0010";
			 			case selector is
			 			when "000" => estado_actual <= s3; 
			 			when "001" => estado_actual <= s4; 
			 			when "010" => estado_actual <= s3; 
			 			when "100" => estado_actual <= s1; 
			 			when "101" => estado_actual <= s0; 
			 			when "110" => estado_actual <= s1; 
			 			when others => null; 
			 			end case; 
					else 
						salida <= "0000";
						estado_actual <= s0;  
					end if;
				
				when s3 => 
			 		if enable = '1' then
			 			salida <= "0110";
			 			case selector is
			 			when "000" => estado_actual <= s4; 
			 			when "001" => estado_actual <= s4; 
			 			when "010" => estado_actual <= s5; 
			 			when "100" => estado_actual <= s2; 
			 			when "101" => estado_actual <= s2; 
			 			when "110" => estado_actual <= s1; 
			 			when others => null; 
			 			end case; 
					else 
						salida <= "0000";
						estado_actual <= s0;  
					end if;
				
				when s4 => 
			 		if enable = '1' then
			 			salida <= "0100";
			 			case selector is
			 			when "000" => estado_actual <= s5; 
			 			when "001" => estado_actual <= s6; 
			 			when "010" => estado_actual <= s5; 
			 			when "100" => estado_actual <= s3; 
			 			when "101" => estado_actual <= s2; 
			 			when "110" => estado_actual <= s3; 
			 			when others => null; 
			 			end case; 
					else 
						salida <= "0000";
						estado_actual <= s0;  
					end if;
				
				when s5 => 
			 		if enable = '1' then
			 			salida <= "1100";
			 			case selector is
			 			when "000" => estado_actual <= s6; 
			 			when "001" => estado_actual <= s6; 
			 			when "010" => estado_actual <= s7; 
			 			when "100" => estado_actual <= s4; 
			 			when "101" => estado_actual <= s4; 
			 			when "110" => estado_actual <= s3; 
			 			when others => null; 
			 			end case; 
					else 
						salida <= "0000";
						estado_actual <= s0;  
					end if;
				
				when s6 => 
			 		if enable = '1' then
			 			salida <= "1000";
			 			case selector is
			 			when "000" => estado_actual <= s7; 
			 			when "001" => estado_actual <= s0; 
			 			when "010" => estado_actual <= s7; 
			 			when "100" => estado_actual <= s5; 
			 			when "101" => estado_actual <= s4; 
			 			when "110" => estado_actual <= s5; 
			 			when others => null; 
			 			end case; 
					else 
						salida <= "0000";
						estado_actual <= s0;  
					end if;
				
				when s7 => 
			 		if enable = '1' then
			 			salida <= "1001";
			 			case selector is
			 			when "000" => estado_actual <= s0; 
			 			when "001" => estado_actual <= s0; 
			 			when "010" => estado_actual <= s1; 
			 			when "100" => estado_actual <= s6; 
			 			when "101" => estado_actual <= s6; 
			 			when "110" => estado_actual <= s5; 
			 			when others => null; 
			 			end case; 
					else 
						salida <= "0000";
						estado_actual <= s0;  
					end if;

				when others => 
					salida <= "0000"; 
					estado_actual <= s0; 
			end case; 
		end if; 
			 			
	end process;

END TypeArchitecture;
